# Fritzing sketch FR_Master (saved by Fritzing 0.9.3b)
circuit board: 22.7387cm x 13.3404cm
breadboards: 1

parts:
  SD_card_module = MicroSD Card Module
  ZS-042_RTC1 = ZS-042 RTC Module
  Part1 = Bluetooth HC-05 Macho
  Part3 = LSM303 Breakout Board - Tilt-Compensated Compass
  Part4 = Arduino Mega 2560 (Rev3)
  S1 = Pushbutton [package="[THT]"]
  R1 = Resistor [tolerance=±5% resistance=2.2k package="0402 [SMD]"]
  C2 = Electrolytic Capacitor [capacitance=0.22mF package="100 mil [THT, electrolytic]"]
  JP3 = Header 5x2 [package=2x5-ra]
  JP4 = Header 5x2 [package=2x5-ra]  # not connected
  U1 = Voltage Regulator - 5V [package="TO220 [THT]"]
  C3 = Ceramic Capacitor [capacitance=100nF package="100 mil [THT, multilayer]"]
  C4 = Electrolytic Capacitor [capacitance=1µF package="100 mil [THT, electrolytic]"]

nets (from the breadboard view):
  GND: SD_card_module.GND, ZS-042_RTC1.GND, Part1.GND, Part3.GND, Part4.GND, R1.Pin_1
  VCC: SD_card_module.VCC, ZS-042_RTC1.VCC, Part1.VCC, Part3.VCC, S1.Pin_1, S1.Pin_2, U1.output_voltage, C3.0, C4.+
  N1: SD_card_module.MISO, Part4.D50
  N2: SD_card_module.MOSI, Part4.D51
  N3: SD_card_module.SCK, Part4.D52
  N4: SD_card_module.CS, Part4.D4_PWM
  N5: ZS-042_RTC1.SDA, Part3.SDA_M, Part4.D20/SDA, Part4.SDA
  N6: ZS-042_RTC1.SCL, Part3.SCL_M, Part4.D21/SCL, Part4.SCL
  N7: Part1.TXD, Part4.D5_PWM
  N8: Part1.RXD, Part4.D6_PWM
  N9: Part4.D8_PWM, S1.Pin_3, S1.Pin_4, R1.Pin_0
  N10: C2.-, JP3.4, U1.GND, C3.1, C4.-
  N11: C2.+, JP3.2, U1.input_voltage
